# Fritzing sketch Fritzing Sketch Source File (saved by Fritzing 0.9.3b)

parts:
  M1 = DC Motor
  S1 = H-Bridge with L298N
  M2 = DC Motor
  Part1 = Arduino Uno (Rev3)
  Part3 = IR Receiver Breakout [package=PCB]
  VCC1 = 4 x AAA Battery Mount

nets:
  N1: M1.pin_1, S1.M2-02
  N2: M1.pin_2, S1.M2-01
  N3: S1.12V, VCC1.+
  GND: S1.GND, Part1.GND, Part3.GND, VCC1.-
  N4: S1.ENA, Part1.D10_PWM/SS
  N5: S1.IN1, Part1.D9_PWM
  N6: S1.IN2, Part1.D8
  N7: S1.IN3, Part1.D7
  N8: S1.IN4, Part1.D6_PWM
  N9: S1.ENB, Part1.D5_PWM
  N10: S1.M1-01, M2.pin_2
  N11: S1.M1-02, M2.pin_1
  N12: Part1.D11_PWM/MOSI, Part3.SIGNAL
  5V: Part1.5V, Part3.VCC

notes:
  Developed By Web Dev Fusion
  https://www.webdevfusion.com
  GND - Green
  VCC - Orange
  GPIO - Blue

custom parts:
  H-Bridge with L298N: h-bridge
  IR Receiver Breakout: Description: This is a very small infrared receiver based on the TSOP85 receiver from Vishay. This receiver has all the filtering and 38kHz demodulation built into the unit. Simply point a IR remote at the receiver, hit a button, and you'll see a stream of 1s and 0s out of the data pin. Documents: Datasheet Schematic Consumer IR Information
